// Logisim project 2's complement.circ as structural Verilog: 1 circuit, main circuit main
// TCMP
module main (
  input  A,
  input  clk,
  input  R,
  output S
);

  wire and_1_out, d_ff_2_q, xor_1_out;

  xor xor_1 (xor_1_out, A, d_ff_2_q);
  // OR_Gate or_1 has open pins: in1=A, in3=d_ff_2_q, out=open
  and and_1 (and_1_out, A, d_ff_2_q);
  D_Flip_Flop d_ff_1 (.clk(clk), .D(xor_1_out), .Q(S), .Qn(R));  // open: preset, en, reset
  D_Flip_Flop d_ff_2 (.clk(clk), .Q(d_ff_2_q), .Qn(R));  // open: D, preset, en, reset
endmodule
