// Logisim project 4 bit comparator.circ as structural Verilog: 1 circuit, main circuit main
module main (
  input  B3,
  input  B2,
  input  B1,
  input  B0,
  output A___4
);

  wire and_1_out, and_2_out, and_3_out, and_4_out, nor_1_out, not_1_out, not_2_out, not_3_out, not_4_out,
       xnor_1_out, xnor_2_out;

  not not_1 (not_1_out, 1'b0);
  not not_2 (not_2_out, 1'b1);
  not not_3 (not_3_out, 1'b0);
  not not_4 (not_4_out, 1'b0);
  nor nor_1 (nor_1_out, 1'b0, B3);
  xnor xnor_1 (xnor_1_out, B2, 1'b1);
  xnor xnor_2 (xnor_2_out, B1, 1'b0);
  and and_1 (and_1_out, not_1_out, B3);
  and and_2 (and_2_out, nor_1_out, not_2_out, B2);
  and and_3 (and_3_out, nor_1_out, xnor_1_out, not_3_out, B1);
  and and_4 (and_4_out, B0, nor_1_out, xnor_1_out, xnor_2_out, not_4_out);
  or or_1 (A___4, and_1_out, and_2_out, and_3_out, and_4_out);
endmodule
