// Logisim project Binary to BCD Converter 16 bit.circ as structural Verilog: 1 circuit, main circuit main
module main (
  input  B15,
  input  B14,
  input  B13,
  input  B12,
  input  B11,
  input  B10,
  input  B9,
  input  B8,
  input  B7,
  input  B6,
  input  B5,
  input  B4,
  input  B3,
  input  B2,
  input  B1,
  input  B0
);
endmodule
