// Logisim project Comparative Adder.circ as structural Verilog: 1 circuit, main circuit main
module main (
  input  I0,
  input  I1,
  input  I2,
  input  I3,
  output O0,
  output O1,
  output O2,
  output O3
);

  wire _4B_Adder_s0, _4B_Adder_s1, _4B_Adder_s2, _4B_Adder_s3, _4B_Comparator_a___4;

  _4_bit_adder_on_logisim_main _4B_Adder (
    .I0(I0), .I1(I1), .I2(I2), .I3(I3), .S0(_4B_Adder_s0), .S1(_4B_Adder_s1), .S2(_4B_Adder_s2),
    .S3(_4B_Adder_s3));
  _4_bit_comparator_main _4B_Comparator (.B3(I3), .B2(I2), .B1(I1), .B0(I0), .A___4(_4B_Comparator_a___4));
  Multiplexer #(.enable("false")) multiplexer_1 (.in0(I0), .in1(_4B_Adder_s0), .out(O0), .sel(_4B_Comparator_a___4));
  Multiplexer #(.enable("false")) multiplexer_2 (.in0(I1), .in1(_4B_Adder_s1), .out(O1), .sel(_4B_Comparator_a___4));
  Multiplexer #(.enable("false")) multiplexer_3 (.in0(I2), .in1(_4B_Adder_s2), .out(O2), .sel(_4B_Comparator_a___4));
  Multiplexer #(.enable("false")) multiplexer_4 (.in0(I3), .in1(_4B_Adder_s3), .out(O3), .sel(_4B_Comparator_a___4));
endmodule
