// Logisim project DoubleDabble.circ as structural Verilog: 1 circuit, main circuit main
module main (
  input  B0,
  input  B1,
  input  B2,
  input  B3,
  input  B4,
  input  B5,
  input  B6,
  input  B7,
  input  B8,
  input  B9,
  input  B10,
  input  B11,
  input  B12,
  input  B13,
  input  B14,
  input  B15,
  output out_17,
  output out_18,
  output out_19,
  output out_20,
  output out_21,
  output out_22,
  output out_23,
  output out_24,
  output out_25,
  output out_26,
  output out_27,
  output out_28,
  output out_29,
  output out_30,
  output out_31,
  output out_32
);

  wire main_1_o0, main_1_o1, main_1_o2, main_1_o3, main_2_o0, main_2_o1, main_2_o2, main_2_o3, main_3_o0,
       main_3_o1, main_3_o2, main_3_o3, main_4_o0, main_4_o1, main_4_o2, main_4_o3, main_5_o0, main_5_o1,
       main_5_o2, main_5_o3, main_6_o0, main_6_o1, main_6_o2, main_6_o3, main_7_o0, main_7_o1, main_7_o2,
       main_7_o3, main_8_o0, main_8_o1, main_8_o2, main_8_o3, main_9_o0, main_9_o1, main_9_o2, main_9_o3,
       main_10_o0, main_10_o1, main_10_o2, main_10_o3, main_11_o0, main_11_o1, main_11_o2, main_11_o3,
       main_12_o0, main_12_o1, main_12_o2, main_12_o3, main_13_o0, main_13_o1, main_13_o2, main_13_o3,
       main_14_o0, main_14_o1, main_14_o2, main_14_o3, main_15_o0, main_15_o1, main_15_o2, main_15_o3,
       main_16_o0, main_16_o1, main_16_o2, main_16_o3, main_17_o0, main_17_o1, main_17_o2, main_17_o3,
       main_18_o0, main_18_o1, main_18_o2, main_18_o3, main_19_o0, main_19_o1, main_19_o2, main_19_o3,
       main_20_o0, main_20_o1, main_20_o2, main_20_o3, main_21_o0, main_21_o1, main_21_o2, main_21_o3,
       main_22_o0, main_22_o1, main_22_o2, main_22_o3, main_23_o0, main_23_o1, main_23_o2, main_23_o3,
       main_24_o0, main_24_o1, main_24_o2, main_24_o3, main_25_o0, main_25_o1, main_25_o2, main_25_o3,
       main_26_o0, main_26_o1, main_26_o2, main_26_o3, main_27_o0, main_27_o1, main_27_o2, main_27_o3,
       main_28_o0, main_28_o1, main_28_o2, main_28_o3, main_29_o0, main_29_o1, main_29_o2, main_29_o3,
       main_30_o0, main_30_o1, main_30_o2, main_30_o3;

  Comparative_Adder_main main_1 (
    .I0(B13), .I1(B14), .I2(B15), .I3(1'b0), .O0(main_1_o0), .O1(main_1_o1), .O2(main_1_o2), .O3(main_1_o3));
  Comparative_Adder_main main_2 (
    .I0(B11), .I1(main_3_o0), .I2(main_3_o1), .I3(main_3_o2), .O0(main_2_o0), .O1(main_2_o1), .O2(main_2_o2),
    .O3(main_2_o3));
  Comparative_Adder_main main_3 (
    .I0(B12), .I1(main_1_o0), .I2(main_1_o1), .I3(main_1_o2), .O0(main_3_o0), .O1(main_3_o1), .O2(main_3_o2),
    .O3(main_3_o3));
  Comparative_Adder_main main_4 (
    .I0(B9), .I1(main_5_o0), .I2(main_5_o1), .I3(main_5_o2), .O0(main_4_o0), .O1(main_4_o1), .O2(main_4_o2),
    .O3(main_4_o3));
  Comparative_Adder_main main_5 (
    .I0(B10), .I1(main_2_o0), .I2(main_2_o1), .I3(main_2_o2), .O0(main_5_o0), .O1(main_5_o1), .O2(main_5_o2),
    .O3(main_5_o3));
  Comparative_Adder_main main_6 (
    .I0(main_5_o3), .I1(main_7_o0), .I2(main_7_o1), .I3(main_7_o2), .O0(main_6_o0), .O1(main_6_o1),
    .O2(main_6_o2), .O3(main_6_o3));
  Comparative_Adder_main main_7 (
    .I0(main_2_o3), .I1(main_3_o3), .I2(main_1_o3), .I3(1'b0), .O0(main_7_o0), .O1(main_7_o1),
    .O2(main_7_o2), .O3(main_7_o3));
  Comparative_Adder_main main_8 (
    .I0(B8), .I1(main_4_o0), .I2(main_4_o1), .I3(main_4_o2), .O0(main_8_o0), .O1(main_8_o1), .O2(main_8_o2),
    .O3(main_8_o3));
  Comparative_Adder_main main_9 (
    .I0(main_4_o3), .I1(main_6_o0), .I2(main_6_o1), .I3(main_6_o2), .O0(main_9_o0), .O1(main_9_o1),
    .O2(main_9_o2), .O3(main_9_o3));
  Comparative_Adder_main main_10 (
    .I0(B6), .I1(main_11_o0), .I2(main_11_o1), .I3(main_11_o2), .O0(main_10_o0), .O1(main_10_o1),
    .O2(main_10_o2), .O3(main_10_o3));
  Comparative_Adder_main main_11 (
    .I0(B7), .I1(main_8_o0), .I2(main_8_o1), .I3(main_8_o2), .O0(main_11_o0), .O1(main_11_o1),
    .O2(main_11_o2), .O3(main_11_o3));
  Comparative_Adder_main main_12 (
    .I0(main_11_o3), .I1(main_13_o0), .I2(main_13_o1), .I3(main_13_o2), .O0(main_12_o0), .O1(main_12_o1),
    .O2(main_12_o2), .O3(main_12_o3));
  Comparative_Adder_main main_13 (
    .I0(main_8_o3), .I1(main_9_o0), .I2(main_9_o1), .I3(main_9_o2), .O0(main_13_o0), .O1(main_13_o1),
    .O2(main_13_o2), .O3(main_13_o3));
  Comparative_Adder_main main_14 (
    .I0(main_13_o3), .I1(main_15_o0), .I2(main_15_o1), .I3(main_15_o2), .O0(main_14_o0), .O1(main_14_o1),
    .O2(main_14_o2), .O3(main_14_o3));
  Comparative_Adder_main main_15 (
    .I0(main_9_o3), .I1(main_6_o3), .I2(main_7_o3), .I3(1'b0), .O0(main_15_o0), .O1(main_15_o1),
    .O2(main_15_o2), .O3(main_15_o3));
  Comparative_Adder_main main_16 (
    .I0(B5), .I1(main_10_o0), .I2(main_10_o1), .I3(main_10_o2), .O0(main_16_o0), .O1(main_16_o1),
    .O2(main_16_o2), .O3(main_16_o3));
  Comparative_Adder_main main_17 (
    .I0(main_10_o3), .I1(main_12_o0), .I2(main_12_o1), .I3(main_12_o2), .O0(main_17_o0), .O1(main_17_o1),
    .O2(main_17_o2), .O3(main_17_o3));
  Comparative_Adder_main main_18 (
    .I0(main_12_o3), .I1(main_14_o0), .I2(main_14_o1), .I3(main_14_o2), .O0(main_18_o0), .O1(main_18_o1),
    .O2(main_18_o2), .O3(main_18_o3));
  Comparative_Adder_main main_19 (
    .I0(B4), .I1(main_16_o0), .I2(main_16_o1), .I3(main_16_o2), .O0(main_19_o0), .O1(main_19_o1),
    .O2(main_19_o2), .O3(main_19_o3));
  Comparative_Adder_main main_20 (
    .I0(main_16_o3), .I1(main_17_o0), .I2(main_17_o1), .I3(main_17_o2), .O0(main_20_o0), .O1(main_20_o1),
    .O2(main_20_o2), .O3(main_20_o3));
  Comparative_Adder_main main_21 (
    .I0(main_17_o3), .I1(main_18_o0), .I2(main_18_o1), .I3(main_18_o2), .O0(main_21_o0), .O1(main_21_o1),
    .O2(main_21_o2), .O3(main_21_o3));
  Comparative_Adder_main main_22 (
    .I0(main_18_o3), .I1(main_14_o3), .I2(main_15_o3), .I3(1'b0), .O0(main_22_o0), .O1(main_22_o1),
    .O2(main_22_o2), .O3(main_22_o3));
  Comparative_Adder_main main_23 (
    .I0(B3), .I1(main_19_o0), .I2(main_19_o1), .I3(main_19_o2), .O0(main_23_o0), .O1(main_23_o1),
    .O2(main_23_o2), .O3(main_23_o3));
  Comparative_Adder_main main_24 (
    .I0(main_19_o3), .I1(main_20_o0), .I2(main_20_o1), .I3(main_20_o2), .O0(main_24_o0), .O1(main_24_o1),
    .O2(main_24_o2), .O3(main_24_o3));
  Comparative_Adder_main main_25 (
    .I0(main_20_o3), .I1(main_21_o0), .I2(main_21_o1), .I3(main_21_o2), .O0(main_25_o0), .O1(main_25_o1),
    .O2(main_25_o2), .O3(main_25_o3));
  Comparative_Adder_main main_26 (
    .I0(main_21_o3), .I1(main_22_o0), .I2(main_22_o1), .I3(main_22_o2), .O0(main_26_o0), .O1(main_26_o1),
    .O2(main_26_o2), .O3(main_26_o3));
  Comparative_Adder_main main_27 (
    .I0(B2), .I1(main_23_o0), .I2(main_23_o1), .I3(main_23_o2), .O0(main_27_o0), .O1(main_27_o1),
    .O2(main_27_o2), .O3(main_27_o3));
  Comparative_Adder_main main_28 (
    .I0(main_23_o3), .I1(main_24_o0), .I2(main_24_o1), .I3(main_24_o2), .O0(main_28_o0), .O1(main_28_o1),
    .O2(main_28_o2), .O3(main_28_o3));
  Comparative_Adder_main main_29 (
    .I0(main_24_o3), .I1(main_25_o0), .I2(main_25_o1), .I3(main_25_o2), .O0(main_29_o0), .O1(main_29_o1),
    .O2(main_29_o2), .O3(main_29_o3));
  Comparative_Adder_main main_30 (
    .I0(main_25_o3), .I1(main_26_o0), .I2(main_26_o1), .I3(main_26_o2), .O0(main_30_o0), .O1(main_30_o1),
    .O2(main_30_o2), .O3(main_30_o3));
  Comparative_Adder_main main_31 (
    .I0(B1), .I1(main_27_o0), .I2(main_27_o1), .I3(main_27_o2), .O0(out_18), .O1(out_19), .O2(out_20),
    .O3(out_21));
  Comparative_Adder_main main_32 (
    .I0(main_27_o3), .I1(main_28_o0), .I2(main_28_o1), .I3(main_28_o2), .O0(out_22), .O1(out_23),
    .O2(out_24), .O3(out_25));
  Comparative_Adder_main main_33 (
    .I0(main_28_o3), .I1(main_29_o0), .I2(main_29_o1), .I3(main_29_o2), .O0(out_26), .O1(out_27),
    .O2(out_28), .O3(out_29));
  Comparative_Adder_main main_34 (
    .I0(main_29_o3), .I1(main_30_o0), .I2(main_30_o1), .I3(main_30_o2), .O0(out_30), .O1(out_31), .O2(out_32));  // open: O3
  Comparative_Adder_main main_35 (
    .I0(main_30_o3), .I1(main_26_o3), .I2(main_22_o3), .I3(1'b0));  // open: O0, O1, O2, O3

  assign out_17 = B0;
endmodule
