// Logisim project half adder as well as CSA.circ as structural Verilog: 2 circuits, main circuit main
// CSADD
module main (
  input  X,
  input  Y,
  input  RST,
  input  clk,
  output SUM
);

  wire and_2_out, AND_out, d_ff_2_q, half_adder_1_c, half_adder_1_sum, not_1_out, not_2_out, xor_2_out,
       XOR_out;

  Half_Adder half_adder_1 (.A(Y), .B(d_ff_2_q), .c(half_adder_1_c), .sum(half_adder_1_sum));
  and AND (AND_out, X, half_adder_1_sum);
  xor XOR (XOR_out, X, half_adder_1_sum);
  not not_1 (not_1_out, RST);
  D_Flip_Flop d_ff_1 (.clk(clk), .D(XOR_out), .Q(SUM), .reset(not_1_out));  // open: Qn, preset, en
  and and_2 (and_2_out, AND_out, half_adder_1_c);
  xor xor_2 (xor_2_out, AND_out, half_adder_1_c);
  D_Flip_Flop d_ff_2 (.clk(clk), .D(xor_2_out), .Q(d_ff_2_q), .reset(not_2_out));  // open: Qn, preset, en
  not not_2 (not_2_out, RST);
endmodule

// HA
module Half_Adder (
  input  A,
  input  B,
  output c,
  output sum
);

  and and_1 (c, A, B);
  xor xor_1 (sum, A, B);
endmodule
