// Logisim project logisim for dd1 project.circ as structural Verilog: 1 circuit, main circuit main
module main (
  input  X_7,
  input  X_6,
  input  X_5,
  input  X_4,
  input  X_3,
  input  X_2,
  input  X_1,
  input  x_0,
  input  Y,
  input  RST,
  input  CLK,
  output PROD
);

  wire and_1_out, and_2_out, and_3_out, and_4_out, and_5_out, and_6_out, and_7_out, and_8_out, main_1_s,
       main_2_sum, main_3_sum, main_4_sum, main_5_sum, main_6_sum, main_7_sum;

  and and_1 (and_1_out, X_7, Y);
  _2_s_complement_main main_1 (.A(and_1_out), .clk(CLK), .R(RST), .S(main_1_s));
  and and_2 (and_2_out, X_6, Y);
  half_adder_as_well_as_CSA_main main_2 (.X(and_2_out), .Y(main_1_s), .RST(RST), .clk(CLK), .SUM(main_2_sum));
  and and_3 (and_3_out, X_5, Y);
  half_adder_as_well_as_CSA_main main_3 (.X(and_3_out), .Y(main_2_sum), .RST(RST), .clk(CLK), .SUM(main_3_sum));
  and and_4 (and_4_out, Y, X_4);
  half_adder_as_well_as_CSA_main main_4 (.X(and_4_out), .Y(main_3_sum), .RST(RST), .clk(CLK), .SUM(main_4_sum));
  and and_5 (and_5_out, X_3, Y);
  half_adder_as_well_as_CSA_main main_5 (.X(and_5_out), .Y(main_4_sum), .RST(RST), .clk(CLK), .SUM(main_5_sum));
  and and_6 (and_6_out, Y, X_2);
  half_adder_as_well_as_CSA_main main_6 (.X(and_6_out), .Y(main_5_sum), .RST(RST), .clk(CLK), .SUM(main_6_sum));
  and and_7 (and_7_out, Y, X_1);
  half_adder_as_well_as_CSA_main main_7 (.X(and_7_out), .Y(main_6_sum), .RST(RST), .clk(CLK), .SUM(main_7_sum));
  and and_8 (and_8_out, Y, x_0);
  half_adder_as_well_as_CSA_main main_8 (.X(and_8_out), .Y(main_7_sum), .RST(RST), .clk(CLK), .SUM(PROD));
endmodule
