// Logisim project logisim for dd1 project.circ as structural Verilog: 1 circuit, main circuit main
module main (
  input  X_7,
  input  X_6,
  input  X_5,
  input  X_4,
  input  X_3,
  input  X_2,
  input  X_1,
  input  x_0,
  input  Y,
  input  RST,
  input  CLK
);

  wire and_1_out, and_2_out, and_3_out, and_4_out, and_5_out, and_6_out, and_7_out, and_8_out, undriven,
       undriven_2, undriven_3, undriven_4, undriven_5, undriven_6, undriven_7;
  wire [7:0] register_1_q, register_2_q, register_3_q, register_4_q, register_5_q, register_6_q,
       register_7_q, register_8_q;

  and and_1 (and_1_out, undriven, Y);
  Register register_1 (.en(CLK), .Q(register_1_q), .clk(RST));  // open: D, clr
  and and_2 (and_2_out, undriven_2, Y);
  Register register_2 (.D(register_1_q), .en(CLK), .Q(register_2_q), .clk(RST));  // open: clr
  and and_3 (and_3_out, undriven_3, Y);
  Register register_3 (.D(register_2_q), .en(CLK), .Q(register_3_q), .clk(RST));  // open: clr
  and and_4 (and_4_out, Y, undriven_4);
  Register register_4 (.D(register_3_q), .en(CLK), .Q(register_4_q), .clk(RST));  // open: clr
  and and_5 (and_5_out, undriven_5, Y);
  Register register_5 (.D(register_4_q), .en(CLK), .Q(register_5_q), .clk(RST));  // open: clr
  and and_6 (and_6_out, Y, undriven_6);
  Register register_6 (.D(register_5_q), .en(CLK), .Q(register_6_q), .clk(RST));  // open: clr
  and and_7 (and_7_out, Y, undriven_7);
  Register register_7 (.D(register_6_q), .en(CLK), .Q(register_7_q), .clk(RST));  // open: clr
  and and_8 (and_8_out, Y, x_0);
  Register register_8 (.D(register_7_q), .en(CLK), .Q(register_8_q), .clk(RST));  // open: clr
endmodule
